# Fritzing sketch circuit_diagram (saved by Fritzing 0.9.6b)
breadboards: 1

parts:
  U1 = NodeMCU V1.0
  Part2 = Arduino Uno (Rev3) - ICSP
  R1 = PHOTOCELL [package=photocell-kit]
  R2 = Resistor [tolerance=±5% resistance=1k package="2010 [SMD]"]
  DHT11_1 = DHT11 module
  Part3 = KY-037 High Sensitivity Sound Detection Module [package="Breakout board"]
  Water_Level_Sensor1 = Water Level Sensor

nets:
  N1: U1.D2, DHT11_1.DATA
  VCC: U1.3V3, R1.P$1, DHT11_1.VCC, Part3.+, Water_Level_Sensor1.VCC
  GND: U1.GND, R2.Pin_1, DHT11_1.GND, Part3.G, Water_Level_Sensor1.GND
  N2: U1.D5, Part2.D5_PWM
  N3: U1.D6, Part2.D6_PWM
  N4: U1.D7, Part2.D9_PWM
  N5: U1.D8, Part2.D10_PWM/SS
  N6: U1.A0, R1.P$2, R2.Pin_0
  N7: Part2.A0, Part3.A0
  N8: Part2.A2, Water_Level_Sensor1.SIG

custom parts:
  NodeMCU V1.0: ESP8266 based NodeMCU
  DHT11 module: https://cdn-learn.adafruit.com/downloads/pdf/dht.pdf DHT11 black pcb module reference by:https://github.com/adafruit/Fritzing-Library/blob/master/parts/DHT11%20Humitidy%20and%20Temperature%20Sensor.fzpz
  KY-037 High Sensitivity Sound Detection Module: KY-037 high sensitivity sound detection module is an analog/digital sensor that uses a condenser microphone to observe changes in environment noise.
  Water Level Sensor: A water level sensor. This sensor operates at 3V to 5V. The Sig (signal) pin outputs an analogue signal that is in proportion to the amount of water in contact with the sensor.
